# Fritzing sketch schema (saved by Fritzing 0.9.3b)
breadboards: 1

parts:
  Composant1 = Arduino Uno (Rev3)
  LED1 = LED - 5mm [color="Red (633nm)" package="5 mm [THT]"]
  LED2 = LED - 5mm [color="Yellow (585nm)" package="5 mm [THT]"]
  LED3 = LED - 5mm [color="Green (560nm)" package="5 mm [THT]"]
  LED4 = LED - 5mm [color="Green (560nm)" package="5 mm [THT]"]
  LED5 = LED - 5mm [color="Red (633nm)" package="5 mm [THT]"]
  S1 = Pushbutton [package="[THT]"]
  Composant2 = Ambient Light Sensor (TEMT6000 Breakout Board)
  R1 = Slide Potentiometer [maximum_resistance=100kΩ]

nets:
  N1: Composant1.A0, S1.Pin_3, S1.Pin_4
  N2: Composant1.A2, Composant2.S
  N3: Composant1.A5/SCL, R1.wiper
  N4: Composant1.D9_PWM, LED1.anode
  N5: Composant1.D10_PWM/SS, LED2.anode
  N6: Composant1.D11_PWM/MOSI, LED3.anode
  GND: Composant1.GND, LED1.cathode, LED2.cathode, LED3.cathode, LED4.cathode, LED5.cathode, Composant2.GND, R1.leg2
  N7: Composant1.D3_PWM, LED5.anode
  N8: Composant1.D5_PWM, LED4.anode
  5V: Composant1.5V, S1.Pin_1, S1.Pin_2, Composant2.VCC, R1.leg1
